# Fritzing sketch MLX90393_ArduinoConnection (saved by Fritzing 0.9.3b)
breadboards: 1

parts:
  Part1 = Arduino Uno (Rev3) - ICSP
  Part2 = Adafruit MLX90393 [part_number="Adafruit #4022"]
  S1 = Pushbutton [package="[THT]"]
  R1 = Resistor [tolerance=±5% resistance=10k package=THT]

nets:
  N1: Part1.A4/SDA, Part2.SDA
  N2: Part1.A5/SCL, Part2.SCL
  N3: Part1.D4, S1.Pin_3, S1.Pin_4, R1.Pin_1
  5V: Part1.5V, Part2.VCC, S1.Pin_1, S1.Pin_2
  GND: Part1.GND, Part2.GND, R1.Pin_0

custom parts:
  Adafruit MLX90393: Measure the invisible magnetic fields that surround us, with this wide-range magnetometer. The MLX90393 is a wide range magnetic field sensor, that can measure 16-bits in ranges from ±5mT up to ±50mT in all 3 axes. Compared to most magnetometers, this gives a huge range, which makes it excellent for detecting magnets and magnetic orientation, rather than the Earth's magnetic field. (Magnets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
